# Fritzing sketch LED-Configuration-System (saved by Fritzing 0.9.4)
breadboards: 1

parts:
  Part1 = Arduino Uno (Rev3) - ICSP
  LED2 = smd LED [color="Green (570nm)" package="0603 [SMD]"]
  LED3 = smd LED [color="Yellow (595nm)" package="0603 [SMD]"]
  R4 = Resistor [tolerance=±5% resistance=150 package="0805 [SMD]"]
  LED5 = DUO LED RG [package="5 mm [THT]"]
  R6 = Resistor [tolerance=±5% resistance=220 package="0805 [SMD]"]
  R7 = Resistor [tolerance=±5% resistance=150 package="0805 [SMD]"]
  LED6 = smd LED [color="Red (633nm)" package="1206 [SMD]"]
  R8 = Resistor [tolerance=±5% resistance=180 package="0805 [SMD]"]
  R3 = Resistor [tolerance=±5% resistance=220 package="0603 [SMD]"]

nets:
  N1: Part1.5V, R4.Pin_1, R6.Pin_0, R7.Pin_1, R8.Pin_1, R3.Pin_1
  N2: Part1.GND, LED2.cathode, LED3.cathode, LED5.common_cathode, LED6.cathode
  N3: LED2.anode, R4.Pin_0
  N4: LED3.anode, R8.Pin_0
  N5: LED5.red_anode, R6.Pin_1
  N6: LED5.green_anode, R7.Pin_0
  N7: LED6.anode, R3.Pin_0

notes:
  Arduino UNO
  220 Ohm
  Red LED
  150 Ohm
  Green LED
  Yellow LED
  180 Ohm
  rg LED
